# Fritzing sketch IntervalometerV2 (saved by Fritzing 0.9.2b)
circuit board: 8.46667cm x 5.64444cm
breadboards: 2

parts:
  Part1 = Arduino Mega 2560 (Rev3)
  MD09B1 = A4988 Stepper Motor Driver Carrier
  Part2 = Arduino Uno (Rev3)
  U1 = Optocoupler [package=THT]
  U2 = Optocoupler [package=THT]  # not connected
  Button_Controller_1 = 3.5mm Audio Jack [package=audio-jack-3.5mm-smd]
  JP1 = RCA [part_number=P package=rca_lock]
  F1 = FUSE [package=fuse_5mm]
  JP2 = RCA [part_number=TORCH package=rca_lock]
  Capacitor_16V200uf = Electrolytic Capacitor [capacitance=200µF voltage=16V package="200 mil [THT, electrolytic]"]
  M1 = Stepper Motor - Unipolar
  Resistor_for_LED_Stepper_Ctrl_STEP = Resistor [tolerance=±5% resistance=560 package="0603 [SMD]"]
  LED_Stepper_Ctrl_STEP = smd LED [color="Green (570nm)" package="0603 [SMD]"]
  LED_Shutter_Trigger = LEDs [package=led10mm]
  LED_Stepper_Ctrl_DIR = smd LED [color="Green (560nm)" package="1206 [SMD]"]
  LED_(yellow) = smd LED [color="Yellow (595nm)" package="0603 [SMD]"]
  Resistor_for_LED_(yellow) = Resistor [tolerance=±1% resistance=1.3k package="0603 [SMD]"]
  Resistor_for_LED_Stepper_Ctrl_DIR = Resistor [tolerance=±1% resistance=1.3k package="0603 [SMD]"]  # not connected
  Resistor_for_LED_Shutter_Trigger = Resistor [tolerance=±5% resistance=560 package="0603 [SMD]"]
  Q1 = PNP-Transistor [package="TO92 [THT]"]
  Q2 = PNP-Transistor [package="TO92 [THT]"]
  R2 = Resistor [tolerance=±1% resistance=110 package=THT]
  R3 = Resistor [tolerance=±1% resistance=110 package=THT]
  JP3 = Header 4 [package=screwterminal-3.5mm-4_lock]
  R4 = Resistor [tolerance=±1% resistance=150 package=THT]
  R5 = Resistor [tolerance=±1% resistance=150 package=THT]

nets (from the breadboard view):
  N1: Part1.A1, Button_Controller_1.LEFT
  N2: Part1.A2, Button_Controller_1.RIGHT
  N3: Part1.D19/RX1, Part2.D1/TX
  N4: Part1.D18/TX1, Part2.D0/RX
  5V: Part1.5V, MD09B1.MS1, MD09B1.MS2, MD09B1.MS3, MD09B1.VDD, Part2.5V
  GND: Part1.GND, MD09B1.GROUND, Part2.GND, Button_Controller_1.SLEEVE, JP1.SHELL, JP2.SHELL, Capacitor_16V200uf.-, Resistor_for_LED_Stepper_Ctrl_STEP.Pin_0, Resistor_for_LED_(yellow).Pin_0, Resistor_for_LED_Shutter_Trigger.Pin_0, R4.Pin_0, R5.Pin_0
  N5: Part1.D4_PWM, U1.Pin_1, LED_(yellow).anode
  N6: Part1.D5_PWM, R3.Pin_0
  N7: Part1.D6_PWM, R2.Pin_0
  N8: Part1.D7_PWM, LED_Shutter_Trigger.C
  N9: MD09B1.RESET, Part2.D8
  N10: MD09B1.STEP, Part2.D4, LED_Stepper_Ctrl_STEP.anode
  N11: MD09B1.DIR, Part2.D7, LED_Stepper_Ctrl_DIR.anode
  N12: MD09B1.VMOT, Part2.VIN, Capacitor_16V200uf.+
  N13: MD09B1.OUT_2B, M1.A
  N14: MD09B1.OUT_2A, M1.COMMON_1
  N15: MD09B1.OUT_1A, M1.C
  N16: MD09B1.OUT_1B, M1.B
  N17: U1.Pin_2, R4.Pin_1
  N18: U1.Pin_4, JP3.3
  N19: U1.Pin_5, JP3.1
  N20: JP1.PIN, Q2.C
  N21: F1.2, Q1.E, Q2.E
  N22: JP2.PIN, Q1.C
  N23: Resistor_for_LED_Stepper_Ctrl_STEP.Pin_1, LED_Stepper_Ctrl_STEP.cathode
  N24: LED_Shutter_Trigger.A, Resistor_for_LED_Shutter_Trigger.Pin_1
  N25: LED_(yellow).cathode, Resistor_for_LED_(yellow).Pin_1
  N26: Q1.B, R3.Pin_1
  N27: Q2.B, R2.Pin_1
